# Fritzing sketch Arduino-TMP36 (saved by Fritzing 0.9.3b)
breadboards: 1

parts:
  Part1 = Arduino Nano (Rev3.0)
  U1 = TMP36 [package=to-92-kit]

nets:
  GND: Part1.GND, U1.GND
  5V: Part1.5V, U1.VCC
  N1: Part1.A0, U1.VOUT
